# Fritzing sketch schema (saved by Fritzing 0.9.3b)
circuit board: 8.46667cm x 5.64444cm

parts:
  Part1 = Arduino Nano (Rev3.0)
  Part2 = BH1750
  electronicsguy1 = electronicsguy 0.96" 128x64 SPI I2C OLED
  Minus = Pushbutton [package="[THT]"]
  Plus = Pushbutton [package="[THT]"]
  Priority = Pushbutton [package="[THT]"]
  Menu = Pushbutton [package="[THT]"]
  Metering = Pushbutton [package="[THT]"]
  Metering_Mode = Pushbutton [package="[THT]"]
  VCC1 = Battery

nets:
  N1: Part1.D2, Metering.Pin_1, Metering.Pin_2
  N2: Part1.D3, Plus.Pin_1, Plus.Pin_2
  N3: Part1.D4, Minus.Pin_1, Minus.Pin_2
  N4: Part1.D5, Priority.Pin_1
  N5: Part1.D6, Menu.Pin_1, Menu.Pin_2
  N6: Part1.D7, Metering_Mode.Pin_1
  N7: Part1.D8, electronicsguy1.D0
  N8: Part1.D9, electronicsguy1.D1
  N9: Part1.D10, electronicsguy1.RST
  N10: Part1.D11/MOSI, electronicsguy1.DC
  N11: Part1.D12/MISO, electronicsguy1.CS
  GND: Part1.GND, Part2.GND, electronicsguy1.GND, Minus.Pin_4, Plus.Pin_3, Plus.Pin_4, Priority.Pin_3, Priority.Pin_4, Menu.Pin_3, Menu.Pin_4, Metering.Pin_3, Metering.Pin_4, Metering_Mode.Pin_3, Metering_Mode.Pin_4, VCC1.-
  5V: Part1.5V, electronicsguy1.VCC, VCC1.+
  N12: Part1.A5, Part2.SCL
  N13: Part1.A4, Part2.SDA
  3V3: Part1.3V3, Part2.VCC

custom parts:
  BH1750: Light Sensor
  electronicsguy 0.96" 128x64 SPI I2C OLED: Generic 0.96" 128x64 SPI I2C OLED Default is SPI mode Can be re-configured for I2C (needs soldering work) Comes in various colors like blue, white, yellow-blue
